# Fritzing sketch Bus (saved by Fritzing 0.9.3b)

parts:
  Part1 = Arduino Uno (Rev3) - ICSP [part_number=uno]
  Part2 = RFID-RC522-v3
  WeMos_D1_Mini1 = WeMos D1 Mini [part_number=wemos]

nets:
  N1: Part1.D0/RX, WeMos_D1_Mini1.TX
  N2: Part1.D1/TX, WeMos_D1_Mini1.RX
  N3: Part2.SDA, WeMos_D1_Mini1.D8
  N4: Part2.SCK, WeMos_D1_Mini1.D5
  N5: Part2.MOSI, WeMos_D1_Mini1.D7
  N6: Part2.MISO, WeMos_D1_Mini1.D6
  N7: Part2.GND, WeMos_D1_Mini1.G
  N8: Part2.RST, WeMos_D1_Mini1.D3
  3.3V: Part2.3.3V, WeMos_D1_Mini1.3V3

custom parts:
  RFID-RC522-v3: A simple China made RFID-RC522 Reader (6x4 cm); do check the pin labels, as this is a MFRC522 based clone.
